# Fritzing sketch Mapper85_DonkeyKongCountry4VRC7 (saved by Fritzing 1.0.3b)
circuit board: 9.00001cm x 5.68cm
breadboards: 1

parts:
  1-30 = Generic single row SMD female header - 30 pins [form="♀ (female)" package=THT]
  60-31 = Generic single row SMD female header - 30 pins [form="♀ (female)" package=THT]
  3_58MHz = Crystal [frequency="16 Mhz" package=SMD]
  LM358 = LM 358 Dual Op-Amp [package="DIP8 [THT]"]
  LM359 = LM 358 Dual Op-Amp [package="SO 08 [SMD]"]
  27K = Resistor [tolerance=±5% power=0.25W resistance=220 package=THT]
  IC2 = IC, DIP package, 32 pins [chip_label=IC]
  2_2K = Resistor [tolerance=±5% power=0.25W resistance=220 package=THT]
  4_7nF = Ceramic Capacitor [capacitance=100nF voltage=35V package="100 mil [THT, multilayer]"]
  33K = Resistor [tolerance=±5% power=0.25W resistance=220 package=THT]
  1uF = Ceramic Capacitor [capacitance=100nF voltage=35V package="100 mil [THT, multilayer]"]
  22uF = Ceramic Capacitor [capacitance=100nF voltage=35V package="100 mil [THT, multilayer]"]
  4_3K = Resistor [tolerance=±5% power=0.25W resistance=220 package=THT]
  240K = Resistor [tolerance=±5% power=0.25W resistance=220 package=THT]
  910 = Resistor [tolerance=±5% power=0.25W resistance=220 package=THT]
  3_9K = Resistor [tolerance=±5% power=0.25W resistance=220 package=THT]
  2_2K_2 = Resistor [tolerance=±5% power=0.25W resistance=220 package=THT]
  IC3 = IC, DIP package, 32 pins [chip_label=IC]
  VRC7 = IC, DIP package, 48 pins [chip_label=IC]

nets:
  N1: 1-30.pin1, IC3.pin16
  N2: 1-30.pin9, VRC7.pin19
  N3: 1-30.pin16, LM358.connector3, LM359.connector3, 2_2K.Pin_0, 4_7nF.1, 33K.Pin_0, 1uF.0, 22uF.1, 910.Pin_1, VRC7.pin46
  N4: 1-30.pin30, LM358.connector4, LM358.connector5, LM358.connector7, LM359.connector4, LM359.connector5, LM359.connector7, 1uF.1, VRC7.pin42
  N5: 60-31.pin6, VRC7.pin33
  N6: 60-31.pin7, VRC7.pin32
  N7: 60-31.pin8, VRC7.pin31
  N8: 60-31.pin15, 3_9K.Pin_0, 2_2K_2.Pin_1
  N9: 60-31.pin16, 3_9K.Pin_1
  N10: 60-31.pin17, VRC7.pin45
  N11: 60-31.pin26, VRC7.pin29
  N12: 60-31.pin27, VRC7.pin28
  N13: 60-31.pin28, VRC7.pin27
  N14: 60-31.pin29, VRC7.pin47
  N15: 3_58MHz.pin_0, VRC7.pin18
  N16: 3_58MHz.pin_1, VRC7.pin17
  N17: LM358.connector0, LM359.connector0, 240K.Pin_1, 910.Pin_0, 2_2K_2.Pin_0
  N18: LM358.connector1, LM359.connector1, 4_3K.Pin_0, 240K.Pin_0
  N19: LM358.connector2, LM359.connector2, 27K.Pin_0, 4_7nF.0, 33K.Pin_1
  N20: LM358.connector6, LM359.connector6
  N21: 27K.Pin_1, 2_2K.Pin_1, VRC7.pin43
  N22: IC2.pin2, VRC7.pin40
  N23: IC2.pin3, VRC7.pin39
  N24: IC2.pin4, VRC7.pin36
  N25: IC2.pin23, VRC7.pin34
  N26: IC2.pin25, VRC7.pin35
  N27: IC2.pin28, VRC7.pin37
  N28: IC2.pin29, VRC7.pin38
  N29: IC2.pin30, VRC7.pin41
  N30: 22uF.0, 4_3K.Pin_1
  N31: IC3.pin2, VRC7.pin23
  N32: IC3.pin3, VRC7.pin22
  N33: IC3.pin22, VRC7.pin44
  N34: IC3.pin28, VRC7.pin20
  N35: IC3.pin29, VRC7.pin21
  N36: IC3.pin30, VRC7.pin25
  N37: IC3.pin31, VRC7.pin26

notes:
  4 VRC7 Hack Repro PCB
  Designed by HeeminYT

custom parts:
  Generic single row SMD female header - 30 pins: Generic single row SMD female header
